// Logisim project 1vhdl.circ as structural Verilog
module main (
  input  in_1,
  input  in_2,
  input  in_3,
  input  in_4,
  output out_5,
  output out_6
);

  p1 p1_1 (.a(in_1), .b(in_2), .c(in_3), .d(in_4), .out1(out_5), .out2(out_6));
endmodule

// VHDL entity p1, as the project stores it:
library ieee;
use ieee.std_logic_1164.all;

entity p1 is
    port (
        a    : in  std_logic;
        b    : in  std_logic;
        c    : in  std_logic;
        d    : in  std_logic;
        out1 : out std_logic;
        out2 : out std_logic
    );
end entity p1;

architecture behavioral of p1 is
begin
    out1 <= a and b and c and d;
    out2 <= a or b or c or d;
end architecture behavioral;
