// Logisim project 2vhdl.circ as structural Verilog
module main (
  input  d0,
  input  d1,
  input  d2,
  input  d3,
  input  d4,
  input  d5,
  input  d6,
  input  d7,
  input  [2:0] s,
  output y
);

  p2 p2_1 (.d0(d0), .d1(d1), .d2(d2), .d3(d3), .d4(d4), .d5(d5), .d6(d6), .d7(d7), .s(s), .y(y));
endmodule

// VHDL entity p2, as the project stores it:
library ieee;
use ieee.std_logic_1164.all;

entity p2 is
    port (
        d0 : in  std_logic;
        d1 : in  std_logic;
        d2 : in  std_logic;
        d3 : in  std_logic;
        d4 : in  std_logic;
        d5 : in  std_logic;
        d6 : in  std_logic;
        d7 : in  std_logic;
        s  : in  std_logic_vector(2 downto 0);
        y  : out std_logic
    );
end entity p2;

architecture behavioral of p2 is
begin
    with s select
        y <= d0 when "000",
             d1 when "001",
             d2 when "010",
             d3 when "011",
             d4 when "100",
             d5 when "101",
             d6 when "110",
             d7 when "111",
             'X' when others;
end architecture behavioral;
