// Logisim project 3vhdl.circ as structural Verilog
module main (
  input  [2:0] x
);

  wire p3_1_a, p3_1_b, p3_1_c, p3_1_d, p3_1_e, p3_1_f, p3_1_g;

  p3 p3_1 (.x(x), .a(p3_1_a), .b(p3_1_b), .c(p3_1_c), .d(p3_1_d), .e(p3_1_e), .f(p3_1_f), .g(p3_1_g));
  _7_Segment_Display u_7_segment_display_1 (
    .g(p3_1_g), .f(p3_1_f), .a(p3_1_a), .b(p3_1_b), .e(p3_1_e), .d(p3_1_d), .c(p3_1_c));  // open: dp
endmodule

// VHDL entity p3, as the project stores it:
library ieee;
use ieee.std_logic_1164.all;

entity p3 is
    port (
        x : in  std_logic_vector(2 downto 0);
        a : out std_logic;
        b : out std_logic;
        c : out std_logic;
        d : out std_logic;
        e : out std_logic;
        f : out std_logic;
        g : out std_logic
    );
end entity p3;

architecture behavioral of p3 is
    signal seg : std_logic_vector(6 downto 0);  -- a b c d e f g
begin
    with x select
        seg <= "1110111" when "000",  -- A
               "0011111" when "001",  -- b
               "1001110" when "010",  -- C
               "0111101" when "011",  -- d
               "1000111" when "100",  -- F
               "1011110" when "101",  -- G
               "0000000" when others;

    a <= seg(6);
    b <= seg(5);
    c <= seg(4);
    d <= seg(3);
    e <= seg(2);
    f <= seg(1);
    g <= seg(0);
end architecture behavioral;
