// Logisim project 4vhdl.circ as structural Verilog
module main (
  input  [24:0] in_1,
  output out_2,
  output [4:0] out_3
);

  p4 p4_1 (.v(in_1), .pass(out_2), .cnt(out_3));
endmodule

// VHDL entity p4, as the project stores it:
library ieee;
use ieee.std_logic_1164.all;
use ieee.numeric_std.all;

entity p4 is
    port (
        v    : in  std_logic_vector(24 downto 0);
        pass : out std_logic;
        cnt  : out std_logic_vector(4 downto 0)
    );
end entity p4;

architecture behavioral of p4 is
begin
    process (v)
        variable n : integer range 0 to 25;
    begin
        n := 0;
        for i in 0 to 24 loop
            if v(i) = '1' then
                n := n + 1;
            end if;
        end loop;

        cnt <= std_logic_vector(to_unsigned(n, 5));

        if n >= 13 then
            pass <= '1';
        else
            pass <= '0';
        end if;
    end process;
end architecture behavioral;
