// Logisim project 5vhdl.circ as structural Verilog
module main (
  input  [12:0] in_1,
  input  in_2
);

  wire p5_1_a, p5_1_b, p5_1_c, p5_1_d, p5_1_e, p5_1_f, p5_1_g;

  p5 p5_1 (.vt(in_1), .en(in_2), .a(p5_1_a), .b(p5_1_b), .c(p5_1_c), .d(p5_1_d), .e(p5_1_e), .f(p5_1_f), .g(p5_1_g));
  _7_Segment_Display u_7_segment_display_1 (
    .g(p5_1_g), .f(p5_1_f), .a(p5_1_a), .b(p5_1_b), .e(p5_1_e), .d(p5_1_d), .c(p5_1_c));  // open: dp
endmodule

// VHDL entity p5, as the project stores it:
library ieee;
use ieee.std_logic_1164.all;
use ieee.numeric_std.all;

entity p5 is
    port (
        vt : in  std_logic_vector(12 downto 0);
        en : in  std_logic;
        a  : out std_logic;
        b  : out std_logic;
        c  : out std_logic;
        d  : out std_logic;
        e  : out std_logic;
        f  : out std_logic;
        g  : out std_logic
    );
end entity p5;

architecture behavioral of p5 is
    signal seg : std_logic_vector(6 downto 0);  -- a b c d e f g
begin
    process (vt, en)
        variable n : integer range 0 to 13;
    begin
        n := 0;
        for i in 0 to 12 loop
            if vt(i) = '1' then
                n := n + 1;
            end if;
        end loop;

        if en = '0' then
            seg <= "0000000";
        else
            case n is
                when 0  => seg <= "1111110";  -- 0
                when 1  => seg <= "0110000";  -- 1
                when 2  => seg <= "1101101";  -- 2
                when 3  => seg <= "1111001";  -- 3
                when 4  => seg <= "0110011";  -- 4
                when 5  => seg <= "1011011";  -- 5
                when 6  => seg <= "1011111";  -- 6
                when 7  => seg <= "1110000";  -- 7
                when 8  => seg <= "1111111";  -- 8
                when 9  => seg <= "1111011";  -- 9
                when 10 => seg <= "1110111";  -- A
                when 11 => seg <= "0011111";  -- b
                when 12 => seg <= "1001110";  -- C
                when 13 => seg <= "0111101";  -- d
            end case;
        end if;
    end process;

    a <= seg(6);
    b <= seg(5);
    c <= seg(4);
    d <= seg(3);
    e <= seg(2);
    f <= seg(1);
    g <= seg(0);
end architecture behavioral;
